// Logisim project ALU.circ as structural Verilog: 4 circuits, main circuit main
module main (
  input  [31:0] A,
  input  [31:0] in_2,
  input  [31:0] B,
  input  [3:0] OPERATION,
  output PF,
  output ZF,
  output NF,
  output EQUAL,
  output [31:0] HI
);

  wire and_2_out, comparator_1_lt, comparator_2_lt;
  wire [31:0] ADD, AND, HI_DIV, HI_DIVU, HI_MUL, HI_MULU, LO_DIV, LO_DIVU, LO_MUL, LO_MULU, NOR, OR, S_LESS,
       SUB, U_LESS, XOR;

  MULU mulu_1 (.A(A), .B(B), .LO(LO_MULU), .HI(HI_MULU));
  DIV div_1 (.A(A), .B(B), .LO(LO_DIV), .HI(HI_DIV));
  Multiplier #(.width(32)) multiplier_1 (.a(A), .b(B), .out(LO_MUL), .cout(HI_MUL));  // open: cin
  Divider #(.width(32)) divider_1 (.a(A), .b(B), .out(LO_DIVU), .rem(HI_DIVU));  // open: upper
  Adder #(.width(32)) adder_1 (.a(A), .b(B), .out(ADD));  // open: cin, cout
  Subtractor #(.width(32)) subtractor_1 (.a(A), .b(B), .out(SUB));  // open: bin, bout
  Comparator #(.width(32)) comparator_1 (.a(A), .b(B), .eq(EQUAL), .lt(comparator_1_lt));  // open: gt
  assign S_LESS = {{31{1'b0}}, comparator_1_lt};  // Bit_Extender bit_extender_1
  Comparator #(.width(32)) comparator_2 (.a(A), .b(B), .lt(comparator_2_lt));  // open: gt, eq
  assign U_LESS = {{31{1'b0}}, comparator_2_lt};  // Bit_Extender bit_extender_2
  assign AND = A & B;  // AND_Gate and_1, 32 bits wide
  assign OR = A | B;  // OR_Gate or_1, 32 bits wide
  assign XOR = A ^ B;  // XOR_Gate xor_1, 32 bits wide
  assign NOR = ~(A | B);  // NOR_Gate nor_1, 32 bits wide
  Multiplexer #(.select(4), .width(32), .disabled(0), .enable("false")) multiplexer_1 (
    .in0({32{1'b0}}), .in1(A), .in2(S_LESS), .in3(U_LESS), .in4(LO_MUL), .in5(LO_MULU), .in6(LO_DIV),
    .in7(LO_DIVU), .in8(ADD), .in9(SUB), .in10(AND), .in11(OR), .in12(NOR), .in13(XOR), .out(in_2),
    .sel(OPERATION));  // open: in14, in15
  Multiplexer #(.select(2), .width(32)) multiplexer_2 (
    .in0(HI_MUL), .in1(HI_MULU), .in2(HI_DIV), .in3(HI_DIVU), .out(HI), .sel(OPERATION[1:0]), .en(and_2_out));
  Comparator #(.width(32)) comparator_3 (.a(in_2), .b({32{1'b0}}), .gt(PF), .eq(ZF), .lt(NF));
  and and_2 (and_2_out, OPERATION[2], ~OPERATION[3]);  // AND_Gate

  // Other names for the same wires on the sheet: OP[3:0] = OPERATION
endmodule

// +X
module MULU (
  input  [31:0] A,
  input  [31:0] B,
  output [31:0] LO,
  output [31:0] HI
);

  wire [31:0] adder_1_out, multiplexer_1_out, multiplexer_2_out, multiplier_1_cout;

  Multiplexer #(.width(32), .enable("false")) multiplexer_1 (
    .in0({32{1'b0}}), .in1(A), .out(multiplexer_1_out), .sel(B[31]));
  Multiplexer #(.width(32), .enable("false")) multiplexer_2 (
    .in0({32{1'b0}}), .in1(B), .out(multiplexer_2_out), .sel(A[31]));
  Multiplier #(.width(32)) multiplier_1 (.a(A), .b(B), .out(LO), .cout(multiplier_1_cout));  // open: cin
  Adder #(.width(32)) adder_1 (.a(multiplexer_1_out), .b(multiplexer_2_out), .out(adder_1_out));  // open: cin, cout
  Adder #(.width(32)) adder_2 (.a(multiplier_1_cout), .b(adder_1_out), .out(HI));  // open: cin, cout

  // Notes on the sheet:
  //   INPUTS
  //   MULU
  //   OUTPUTS
endmodule

module DIV (
  input  [31:0] A,
  input  [31:0] LO,
  input  [31:0] HI,
  input  [31:0] B
);

  wire xor_1_out;
  wire [31:0] divider_1_out, multiplexer_1_out, multiplexer_2_out, negator_1_out, negator_2_out,
       negator_3_out;

  Negator #(.width(32)) negator_1 (.in(A), .out(negator_1_out));
  Negator #(.width(32)) negator_2 (.in(B), .out(negator_2_out));
  Multiplexer #(.width(32), .enable("false")) multiplexer_1 (
    .in0(A), .in1(negator_1_out), .out(multiplexer_1_out), .sel(A[31]));
  Multiplexer #(.width(32), .enable("false")) multiplexer_2 (
    .in0(B), .in1(negator_2_out), .out(multiplexer_2_out), .sel(B[31]));
  Divider #(.width(32)) divider_1 (
    .a(multiplexer_1_out), .b(multiplexer_2_out), .out(divider_1_out), .rem(HI));  // open: upper
  xor xor_1 (xor_1_out, A[31], B[31]);
  Negator #(.width(32)) negator_3 (.in(divider_1_out), .out(negator_3_out));
  Multiplexer #(.width(32), .enable("false")) multiplexer_3 (
    .in0(divider_1_out), .in1(negator_3_out), .out(LO), .sel(xor_1_out));

  // Notes on the sheet:
  //   DIV
endmodule

module Register_File (
  input  [31:0] DI,
  input  [31:0] L,
  input  [31:0] H,
  input  [4:0] RD,
  input  [4:0] RS,
  input  [4:0] RT,
  input  CLOCK,
  input  RESET,
  input  LOAD,
  input  SELECT,
  input  [31:0] DRS,
  input  POP_PUSH,
  input  INIT_SP,
  input  [31:0] DRT,
  input  LOAD_SP,
  input  R_W,
  input  [31:0] HI_LO
);

  wire L1, L2, L3, L4, L5, L6, L7, L8, L9, L10, L11, L12, L13, L14, L15, L16, L17, L18, L19, L20, L21, L22,
       L23, L24, L25, L26, L27, L28, L29, L30, LSP, LSP2;
  wire [31:0] adder_1_out, HI, LO, multiplexer_1_out, multiplexer_2_out, N_SP, Q0, Q1, Q2, Q3, Q4, Q5, Q6,
       Q7, Q8, Q9, Q10, Q11, Q12, Q13, Q14, Q15, Q16, Q17, Q18, Q19, Q20, Q21, Q22, Q23, Q24, Q25, Q26, Q27,
       Q28, Q29, Q30, QSP;

  Register #(.width(32)) R0 (.Q(Q0), .clk(CLOCK), .clr(RESET));  // open: D, en
  Register #(.width(32)) R4 (.D(DI), .en(L4), .Q(Q4), .clk(CLOCK), .clr(RESET));
  Register #(.width(32)) R8 (.D(DI), .en(L8), .Q(Q8), .clk(CLOCK), .clr(RESET));
  Register #(.width(32)) R12 (.D(DI), .en(L12), .Q(Q12), .clk(CLOCK), .clr(RESET));
  Register #(.width(32)) R16 (.D(DI), .en(L16), .Q(Q16), .clk(CLOCK), .clr(RESET));
  Register #(.width(32)) R20 (.D(DI), .en(L20), .Q(Q20), .clk(CLOCK), .clr(RESET));
  Register #(.width(32)) R24 (.D(DI), .en(L24), .Q(Q24), .clk(CLOCK), .clr(RESET));
  Register #(.width(32)) R28 (.D(DI), .en(L28), .Q(Q28), .clk(CLOCK), .clr(RESET));
  or or_1 (LSP, LOAD_SP, LSP2);
  Register #(.width(32)) R1 (.D(DI), .en(L1), .Q(Q1), .clk(CLOCK), .clr(RESET));
  Register #(.width(32)) R5 (.D(DI), .en(L5), .Q(Q5), .clk(CLOCK), .clr(RESET));
  Register #(.width(32)) R9 (.D(DI), .en(L9), .Q(Q9), .clk(CLOCK), .clr(RESET));
  Register #(.width(32)) R13 (.D(DI), .en(L13), .Q(Q13), .clk(CLOCK), .clr(RESET));
  Register #(.width(32)) R17 (.D(DI), .en(L17), .Q(Q17), .clk(CLOCK), .clr(RESET));
  Register #(.width(32)) R21 (.D(DI), .en(L21), .Q(Q21), .clk(CLOCK), .clr(RESET));
  Register #(.width(32)) R25 (.D(DI), .en(L25), .Q(Q25), .clk(CLOCK), .clr(RESET));
  Register #(.width(32)) R29 (.D(DI), .en(L29), .Q(Q29), .clk(CLOCK), .clr(RESET));
  Multiplexer #(.width(32)) multiplexer_1 (
    .in0(32'h4), .in1(32'hfffffffc), .out(multiplexer_1_out), .sel(POP_PUSH));  // open: en
  Register #(.width(32)) u_LO (.D(L), .en(LOAD), .Q(LO), .clk(CLOCK), .clr(RESET));
  Adder #(.width(32)) adder_1 (.a(multiplexer_1_out), .b(QSP), .out(adder_1_out));  // open: cin, cout
  Register #(.width(32)) R2 (.D(DI), .en(L2), .Q(Q2), .clk(CLOCK), .clr(RESET));
  Register #(.width(32)) R6 (.D(DI), .en(L6), .Q(Q6), .clk(CLOCK), .clr(RESET));
  Register #(.width(32)) R10 (.D(DI), .en(L10), .Q(Q10), .clk(CLOCK), .clr(RESET));
  Register #(.width(32)) R14 (.D(DI), .en(L14), .Q(Q14), .clk(CLOCK), .clr(RESET));
  Register #(.width(32)) R18 (.D(DI), .en(L18), .Q(Q18), .clk(CLOCK), .clr(RESET));
  Register #(.width(32)) R22 (.D(DI), .en(L22), .Q(Q22), .clk(CLOCK), .clr(RESET));
  Register #(.width(32)) R26 (.D(DI), .en(L26), .Q(Q26), .clk(CLOCK), .clr(RESET));
  Register #(.width(32)) R30 (.D(DI), .en(L30), .Q(Q30), .clk(CLOCK), .clr(RESET));
  Multiplexer #(.width(32)) multiplexer_2 (
    .in0(adder_1_out), .in1(32'h100000), .out(multiplexer_2_out), .sel(INIT_SP));  // open: en
  Multiplexer #(.width(32)) multiplexer_3 (.in0(DI), .in1(multiplexer_2_out), .out(N_SP), .sel(LOAD_SP));  // open: en
  Register #(.width(32)) R3 (.D(DI), .en(L3), .Q(Q3), .clk(CLOCK), .clr(RESET));
  Register #(.width(32)) R7 (.D(DI), .en(L7), .Q(Q7), .clk(CLOCK), .clr(RESET));
  Register #(.width(32)) R11 (.D(DI), .en(L11), .Q(Q11), .clk(CLOCK), .clr(RESET));
  Register #(.width(32)) R15 (.D(DI), .en(L15), .Q(Q15), .clk(CLOCK), .clr(RESET));
  Register #(.width(32)) R19 (.D(DI), .en(L19), .Q(Q19), .clk(CLOCK), .clr(RESET));
  Register #(.width(32)) R23 (.D(DI), .en(L23), .Q(Q23), .clk(CLOCK), .clr(RESET));
  Register #(.width(32)) R27 (.D(DI), .en(L27), .Q(Q27), .clk(CLOCK), .clr(RESET));
  Register #(.width(32)) R31_SP (.D(N_SP), .en(LSP), .Q(QSP), .clk(CLOCK), .clr(RESET));
  Register #(.width(32)) u_HI (.D(H), .en(LOAD), .Q(HI), .clk(CLOCK), .clr(RESET));
  Multiplexer #(.select(5), .width(32)) multiplexer_4 (
    .in0(Q0), .in1(Q1), .in2(Q2), .in3(Q3), .in4(Q4), .in5(Q5), .in6(Q6), .in7(Q7), .in8(Q8), .in9(Q9),
    .in10(Q10), .in11(Q11), .in12(Q12), .in13(Q13), .in14(Q14), .in15(Q15), .in16(Q16), .in17(Q17),
    .in18(Q18), .in19(Q19), .in20(Q20), .in21(Q21), .in22(Q22), .in23(Q23), .in24(Q24), .in25(Q25),
    .in26(Q26), .in27(Q27), .in28(Q28), .in29(Q29), .in30(Q30), .in31(QSP), .out(DRS), .sel(RS));  // open: en
  Multiplexer #(.select(5), .width(32)) multiplexer_5 (
    .in0(Q0), .in1(Q1), .in2(Q2), .in3(Q3), .in4(Q4), .in5(Q5), .in6(Q6), .in7(Q7), .in8(Q8), .in9(Q9),
    .in10(Q10), .in11(Q11), .in12(Q12), .in13(Q13), .in14(Q14), .in15(Q15), .in16(Q16), .in17(Q17),
    .in18(Q18), .in19(Q19), .in20(Q20), .in21(Q21), .in22(Q22), .in23(Q23), .in24(Q24), .in25(Q25),
    .in26(Q26), .in27(Q27), .in28(Q28), .in29(Q29), .in30(Q30), .in31(QSP), .out(DRS), .sel(RT));  // open: en
  Multiplexer #(.width(32)) multiplexer_6 (.in0(HI), .in1(LO), .out(HI_LO), .sel(SELECT));  // open: en
  Demultiplexer #(.select(5)) demultiplexer_1 (
    .out1(L1), .out2(L2), .out3(L3), .out4(L4), .out5(L5), .out6(L6), .out7(L7), .out8(L8), .out9(L9),
    .out10(L10), .out11(L11), .out12(L12), .out13(L13), .out14(L14), .out15(L15), .out16(L16), .out17(L17),
    .out18(L18), .out19(L19), .out20(L20), .out21(L21), .out22(L22), .out23(L23), .out24(L24), .out25(L25),
    .out26(L26), .out27(L27), .out28(L28), .out29(L29), .out30(L30), .out31(LSP2), .in(R_W), .sel(RD));  // open: out0, en

  // Other names for the same wires on the sheet: CLK = CLOCK; I_SP = INIT_SP; LM_D = LOAD; LSP1 = LOAD_SP;
  //   RST = RESET; SELECTOR_H_L = SELECT

  // Notes on the sheet:
  //   INPUTS
  //   DATA IN
  //   LOW AND HIGH
  //   DATA ADRRESS
  //   SELECTOR A
  //   SELECTOR B
  //   CLOCK
  //   RESET
  //   READ/WRITE
  //   OUTPUTS
endmodule
